# Fritzing sketch Project_Schematics (saved by Fritzing 0.9.3b)
breadboards: 1

parts:
  Gizwits_WiFi_Witty_ESP-12F1 = Gizwits WiFi Witty ESP-12F
  WeMos_D1_Mini_Relay_Shield1 = WeMos D1 Mini Relay Shield
  HLK-PM1 = HLK-PM01
  Part1 = Bluetooth HC-05 Macho
  U3 = SWITCH-SPST-2 [package=switch-spst-vertical]
  Part2 = Lilypad Power Supply
  Power_plug1 = Power plug
  LED4 = LEDs [package=led10mm]

nets:
  VCC: Gizwits_WiFi_Witty_ESP-12F1.VCC, WeMos_D1_Mini_Relay_Shield1.3V3, Part1.VCC, U3.O
  N1: Gizwits_WiFi_Witty_ESP-12F1.GPIO2, WeMos_D1_Mini_Relay_Shield1.D2
  N2: Gizwits_WiFi_Witty_ESP-12F1.GPIO0, Part1.TXD
  N3: Gizwits_WiFi_Witty_ESP-12F1.GPIO4, Part1.RXD
  N4: WeMos_D1_Mini_Relay_Shield1.COM, HLK-PM1.AC#1, Power_plug1.VCC
  GND: WeMos_D1_Mini_Relay_Shield1.G, HLK-PM1.-Vo, HLK-PM1.+Vo, Part1.GND, Part2.GND
  N5: WeMos_D1_Mini_Relay_Shield1.NC, LED4.A
  N6: HLK-PM1.AC#0, Power_plug1.GND, LED4.C
  N7: U3.P, Part2.+
